// Logisim project alu-harness.circ as structural Verilog: 1 circuit, main circuit main
module main (
  output [7:0] Test_num,
  output Equal,
  output [15:0] Result,
  output Signed_Overflow,
  output [15:0] Result_2
);

  wire clock_1_out;
  wire [2:0] rom_3_data;
  wire [7:0] adder_1_out;
  wire [15:0] rom_1_data, rom_2_data;

  Clock clock_1 (.out(clock_1_out));
  Adder adder_1 (.a(8'h1), .b(Test_num), .out(adder_1_out));  // open: cin, cout
  Register register_1 (.D(adder_1_out), .Q(Test_num), .clk(clock_1_out));  // open: en, clr
  ROM #(.dataWidth(16)) rom_1 (.addr(Test_num), .data(rom_1_data));  // open: sel
  ROM #(.dataWidth(16)) rom_2 (.addr(Test_num), .data(rom_2_data));  // open: sel
  ROM #(.dataWidth(3)) rom_3 (.addr(Test_num), .data(rom_3_data));  // open: sel
  alu_main main_1 (
    .Switch(rom_3_data), .X(rom_1_data), .Equal(Equal), .Result(Result), .Y(rom_2_data), .Result_2(Result_2),
    .Signed_Overflow(Signed_Overflow));

  // Notes on the sheet:
  //   YOUR ALU SHOULD FIT HERE
  //   There should be no blue/red wires here, and the result shouldn't be x's.
endmodule
