// Logisim project alu.circ as structural Verilog: 3 circuits, main circuit main
module main (
  input  [15:0] X,
  input  [15:0] Y,
  input  [2:0] Switch,
  output Equal,
  output [15:0] Result,
  output [15:0] Result_2,
  output Signed_Overflow
);

  wire comparator_1_eq, comparator_2_lt, comparator_3_eq, overflow;
  wire [3:0] bit_extender_1_out, bit_extender_2_out;
  wire [15:0] adder_1_out, and_1_out, bit_extender_3_out, multiplier_1_cout, multiplier_1_out, or_1_out,
       shifter_1_out, shifter_2_out, signed_add_1_sum;

  Comparator #(.width(3), .mode("unsigned")) comparator_1 (
    .a(Switch), .b(3'b111), .eq(comparator_1_eq));  // open: gt, lt
  Shifter #(.width(16)) shifter_1 (.in(X), .\dist (bit_extender_1_out), .out(shifter_1_out));
  Bit_Extender #(.in_width(16), .out_width(4)) bit_extender_1 (.in(Y), .out(bit_extender_1_out));
  Bit_Extender #(.in_width(16), .out_width(4)) bit_extender_2 (.in(Y), .out(bit_extender_2_out));
  signed_add signed_add_1 (.in_1(X), .in_2(Y), .sum(signed_add_1_sum), .\signed (overflow));
  assign and_1_out = X & Y;  // AND_Gate and_1, 16 bits wide
  assign or_1_out = X | Y;  // OR_Gate or_1, 16 bits wide
  Adder #(.width(16)) adder_1 (.a(X), .b(Y), .out(adder_1_out));  // open: cin, cout
  Comparator #(.width(16)) comparator_2 (.a(X), .b(Y), .eq(Equal), .lt(comparator_2_lt));  // open: gt
  Multiplier #(.width(16)) multiplier_1 (.a(X), .b(Y), .out(multiplier_1_out), .cout(multiplier_1_cout));  // open: cin
  Multiplexer #(.width(16)) multiplexer_1 (
    .in0({16{1'b0}}), .in1(multiplier_1_cout), .out(Result_2), .sel(comparator_1_eq));  // open: en
  Shifter #(.width(16), .shift("lr")) shifter_2 (.in(X), .\dist (bit_extender_2_out), .out(shifter_2_out));
  assign bit_extender_3_out = {{15{comparator_2_lt}}, comparator_2_lt};  // Bit_Extender bit_extender_3
  Multiplexer #(.select(3), .width(16)) multiplexer_2 (
    .in0(shifter_1_out), .in1(shifter_2_out), .in2(signed_add_1_sum), .in3(and_1_out), .in4(or_1_out),
    .in5(adder_1_out), .in6(bit_extender_3_out), .in7(multiplier_1_out), .out(Result), .sel(Switch));  // open: en
  Comparator #(.width(3)) comparator_3 (.a(Switch), .b(3'b010), .eq(comparator_3_eq));  // open: gt, lt
  Multiplexer multiplexer_3 (.in0(1'b0), .in1(overflow), .out(Signed_Overflow), .sel(comparator_3_eq));  // open: en

  // Other names for the same wires on the sheet: S[2:0] = Switch

  // Notes on the sheet:
  //   INPUTS to your circuit
  //   DON'T CHANGE THE LOCATIONS OF THE INPUTS AND OUTPUTS!
  //   OUTPUTS from your circuit
endmodule

module signed_add (
  input  [15:0] in_1,
  input  [15:0] in_2,
  output [15:0] sum,
  output \signed 
);

  wire and_1_out, and_2_out, MA, MB, minus_MA, minus_MB, msb_3_out, not_3_out;

  not not_1 (minus_MA, MA);
  // Probe on minus_MA
  MSB msb_1 (.in_1(in_1), .out(MA));
  Adder #(.width(16)) adder_1 (.a(in_1), .b(in_2), .out(sum));  // open: cin, cout
  // Probe on sum
  not not_2 (minus_MB, MB);
  MSB msb_2 (.in_1(in_2), .out(MB));
  MSB msb_3 (.in_1(sum), .out(msb_3_out));
  // Probe on msb_3_out
  not not_3 (not_3_out, msb_3_out);
  and and_1 (and_1_out, minus_MA, msb_3_out, minus_MB);
  and and_2 (and_2_out, MA, not_3_out, MB);
  // Probe on and_1_out
  // Probe on and_2_out
  or or_1 (\signed , and_1_out, and_2_out);
endmodule

module MSB (
  input  [15:0] in_1,
  output out
);


  assign out = in_1[15];
endmodule
