// Logisim project cpu.circ as structural Verilog: 6 circuits, main circuit main
module main (
  input  [15:0] INSTRUCTION,
  input  CLOCK,
  output [15:0] FETCH_ADDRESS,
  output Overflow,
  output [15:0] s0_Value,
  output [15:0] s1_Value,
  output [15:0] s2_Value,
  output [15:0] ra_Value,
  output [15:0] sp_Value,
  output [15:0] HI_Value,
  output [15:0] LO_Value
);

  wire AluSrc, Branch, ExtOp, JR, Jump, MEM_p1, MEM_p2, MEM_p4, MEM_p10, MEM_p14, MEM_p17, MemW, not_1_out,
       or_1_out, RegDst, RegWr, WE, zero;
  wire [1:0] SrcToR;
  wire [2:0] AluCtr, bit_extender_1_out, func, multiplexer_3_out, rdi, rs_t;
  wire [3:0] _12_15;
  wire [5:3] IImm;
  wire [15:0] Immo, lo_input_1_to_lo, MEM_p11, multiplexer_1_out, multiplexer_4_out, multiplexer_5_out,
       NexIns, next_pc_logic_1_addr_branch_or_next, next_pc_logic_1_jumpaddr, npc, PC, PP2, Re1, Re2, RS, WD,
       WM;

  or or_1 (or_1_out, Jump, JR, Branch);
  LO_Input lo_input_1 (
    .Result1(Re1), .Immediate({rdi[0], rs_t, IImm, func}), .funct(func), .Opt(_12_15),
    .To_LO(lo_input_1_to_lo));
  Multiplexer #(.width(16)) multiplexer_1 (.in0(PP2), .in1(npc), .out(multiplexer_1_out), .sel(or_1_out));  // open: en
  Register #(.width(16)) u_PC (.D(multiplexer_1_out), .Q(FETCH_ADDRESS), .clk(CLOCK));  // open: en, clr
  Register #(.width(16)) HI (.D(Re2), .Q(HI_Value), .clk(CLOCK));  // open: en, clr
  Register #(.width(16)) LO (.D(lo_input_1_to_lo), .Q(LO_Value), .clk(CLOCK));  // open: en, clr
  Adder #(.width(16)) adder_1 (.a(16'h2), .b(FETCH_ADDRESS), .out(PP2));  // open: cin, cout
  Register #(.width(16)) IF_EX (.D(FETCH_ADDRESS), .Q(PC), .clk(CLOCK));  // open: en, clr
  Hazard_Manage hazard_manage_1 (.Instruction(INSTRUCTION), .Jump(Jump), .Zero(zero), .Branch(Branch), .Result(NexIns));
  Register #(.width(16)) IF_EX_2 (.D(NexIns), .Q({_12_15, rdi, rs_t, IImm, func}), .clk(CLOCK));  // open: en, clr
  Multiplexer #(.width(16)) multiplexer_2 (
    .in0(next_pc_logic_1_addr_branch_or_next), .in1(next_pc_logic_1_jumpaddr), .out(npc), .sel(Jump));  // open: en
  Control_Unit control_unit_1 (
    .Inst_12_15(_12_15), .Inst__0_2(func), .JR(JR), .Jump(Jump), .RegDst(RegDst), .ExtOpt(ExtOp),
    .ALUSrc(AluSrc), .ALUCtr(AluCtr), .MemWr(MemW), .SrctoReg(SrcToR), .RegWr(RegWr), .Branch(Branch));
  Next_PC_Logic next_pc_logic_1 (
    .Addr_Branch_or_next(next_pc_logic_1_addr_branch_or_next), .JumpAddr(next_pc_logic_1_jumpaddr), .RS(RS),
    .Zero(zero), .Branch(Branch), .JR(JR), .PC(PC), .UImmediate({rdi[0], rs_t, IImm, func}), .IImm(Immo));
  ExtendImm extendimm_1 (.EIm({IImm, func}), .ExtOp(ExtOp), .Immo(Immo));
  assign bit_extender_1_out = {{1{1'b0}}, rdi[2:1]};  // Bit_Extender bit_extender_1
  Multiplexer #(.width(3)) multiplexer_3 (
    .in0(rdi), .in1(bit_extender_1_out), .out(multiplexer_3_out), .sel(RegDst));  // open: en
  regfile_main main_1 (
    .Read_Register_1(rs_t), .Read_Register_2(IImm), .Write_Register(multiplexer_3_out), .Write_Data(WD),
    .Write_Enable(WE), .Clock(CLOCK), .Read_Data_1(RS), .Read_Data_2(WM), .s0_Value(s0_Value),
    .s1_Value(s1_Value), .s2_Value(s2_Value), .ra_Value(ra_Value), .sp_Value(sp_Value));
  // mem_main MEM: pin names not known; wires that end beside it: MEM_p1, MEM_p2, MEM_p2, MEM_p4, Re1, WM, MemW, MEM_p4, CLOCK, MEM_p10, MEM_p11, AluCtr, MEM_p10, MEM_p14, LO_Value, MEM_p14, MEM_p17, MEM_p17
  alu_main main_2 (
    .Switch(AluCtr), .X(RS), .Equal(zero), .Result(Re1), .Y(multiplexer_4_out), .Result_2(Re2),
    .Signed_Overflow(Overflow));
  Multiplexer #(.width(16)) multiplexer_4 (.in0(WM), .in1(Immo), .out(multiplexer_4_out), .sel(AluSrc));  // open: en
  Multiplexer #(.select(2), .width(16)) multiplexer_5 (
    .in0(Re1), .in1(MEM_p11), .in2(HI_Value), .in3(LO_Value), .out(multiplexer_5_out), .sel(SrcToR));  // open: en
  not not_1 (not_1_out, Overflow);
  Multiplexer #(.width(16)) multiplexer_6 (.in0(multiplexer_5_out), .in1(PP2), .out(WD), .sel(Jump));  // open: en
  buf and_1 (WE, not_1_out);  // AND_Gate

  // Other names for the same wires on the sheet: IImm[2:0] = func; UImm[9:0] = {rdi[0], rs_t, IImm, func};
  //   rt[2:0] = IImm; rdu[1:0] = rdi[2:1]; clk = CLOCK; fetch_addr[15:0] = FETCH_ADDRESS; HI[15:0] = HI_Value;
  //   LO[15:0] = LO_Value; ra[15:0] = ra_Value; s0[15:0] = s0_Value; s1[15:0] = s1_Value; s2[15:0] = s2_Value;
  //   sp[15:0] = sp_Value

  // Notes on the sheet:
  //   Output
  //   These are outputs/inputs from run.circ
  //   Inputs
  //   These are DEBUG/TEST outputs from your circuit.
endmodule

module Next_PC_Logic (
  input  [15:0] IImm,
  input  Zero,
  input  Branch,
  input  JR,
  input  [15:0] PC,
  input  [9:0] UImmediate,
  input  [15:0] RS,
  output [15:0] Addr_Branch_or_next,
  output [15:0] JumpAddr
);

  wire Branch_And_out;
  wire [15:0] adder_1_out, adder_2_out, adder_3_out, adder_4_out, bit_extender_1_out, bit_extender_2_out,
       shifter_1_out;

  assign bit_extender_1_out = {{10{1'b0}}, PC[15:10]};  // Bit_Extender bit_extender_1
  Shifter #(.width(16)) shifter_1 (.in(bit_extender_1_out), .\dist (4'b1010), .out(shifter_1_out));
  assign bit_extender_2_out = {{6{1'b0}}, UImmediate};  // Bit_Extender bit_extender_2
  Adder #(.width(16)) adder_1 (.a(shifter_1_out), .b(bit_extender_2_out), .out(adder_1_out));  // open: cin, cout
  Adder #(.width(16)) adder_2 (.a(IImm), .b(RS), .out(adder_2_out));  // open: cin, cout
  Adder #(.width(16)) adder_3 (.a(PC), .b(16'h2), .out(adder_3_out));  // open: cin, cout
  Adder #(.width(16)) adder_4 (.a(PC), .b(IImm), .out(adder_4_out));  // open: cin, cout
  Multiplexer #(.width(16)) multiplexer_1 (.in0(adder_1_out), .in1(adder_2_out), .out(JumpAddr), .sel(JR));  // open: en
  and Branch_And (Branch_And_out, Zero, Branch);
  Multiplexer #(.width(16)) multiplexer_2 (
    .in0(adder_3_out), .in1(adder_4_out), .out(Addr_Branch_or_next), .sel(Branch_And_out));  // open: en

  // Other names for the same wires on the sheet: Addr[15:0] = Addr_Branch_or_next
endmodule

module Control_Unit (
  input  [2:0] Inst__0_2,
  input  [3:0] Inst_12_15,
  output JR,
  output Jump,
  output RegDst,
  output ExtOpt,
  output ALUSrc,
  output [2:0] ALUCtr,
  output MemWr,
  output [1:0] SrctoReg,
  output RegWr,
  output Branch
);

  wire and_1_out, and_2_out, and_3_out, and_4_out, comparator_2_eq, comparator_3_eq, comparator_4_eq,
       comparator_5_eq, comparator_6_eq, comparator_7_eq, comparator_8_eq, comparator_10_eq,
       comparator_11_eq, comparator_12_eq, comparator_13_eq, comparator_14_eq, comparator_15_eq,
       comparator_16_eq, comparator_17_eq, comparator_18_eq, comparator_19_eq, comparator_20_eq,
       comparator_21_eq, comparator_22_eq, comparator_23_eq, comparator_24_eq, not_1_out, not_2_out,
       not_3_out, not_4_out, or_4_out, or_6_out, or_7_out, or_10_out;
  wire [2:0] or_9_out;

  not not_1 (not_1_out, Inst_12_15[2]);
  not not_2 (not_2_out, Inst_12_15[3]);
  Comparator #(.width(4), .mode("unsigned")) comparator_1 (.a(Inst_12_15), .b(4'b0011), .eq(JR));  // open: gt, lt
  Comparator #(.width(4), .mode("unsigned")) comparator_2 (
    .a(Inst_12_15), .b(4'b0011), .eq(comparator_2_eq));  // open: gt, lt
  Comparator #(.width(4), .mode("unsigned")) comparator_3 (
    .a(Inst_12_15), .b(4'b0010), .eq(comparator_3_eq));  // open: gt, lt
  Comparator #(.width(4), .mode("unsigned")) comparator_4 (
    .a(Inst_12_15), .b(4'b0001), .eq(comparator_4_eq));  // open: gt, lt
  Comparator #(.width(4), .mode("unsigned")) comparator_5 (
    .a(Inst_12_15), .b(4'b0010), .eq(comparator_5_eq));  // open: gt, lt
  Comparator #(.width(4), .mode("unsigned")) comparator_6 (
    .a(Inst_12_15), .b(4'b1001), .eq(comparator_6_eq));  // open: gt, lt
  Comparator #(.width(4), .mode("unsigned")) comparator_7 (
    .a(Inst_12_15), .b(4'b1010), .eq(comparator_7_eq));  // open: gt, lt
  Comparator #(.width(4), .mode("unsigned")) comparator_8 (
    .a(Inst_12_15), .b(4'b0000), .eq(comparator_8_eq));  // open: gt, lt
  not not_3 (not_3_out, Inst_12_15[1]);
  not not_4 (not_4_out, Inst_12_15[0]);
  Comparator #(.width(4), .mode("unsigned")) comparator_9 (.a(Inst_12_15), .b(4'b1100), .eq(MemWr));  // open: gt, lt
  Comparator #(.width(4), .mode("unsigned")) comparator_10 (
    .a(Inst_12_15), .b(4'b0000), .eq(comparator_10_eq));  // open: gt, lt
  Comparator #(.width(4), .mode("unsigned")) comparator_11 (
    .a(Inst_12_15), .b(4'b0110), .eq(comparator_11_eq));  // open: gt, lt
  Comparator #(.width(4), .mode("unsigned")) comparator_12 (
    .a(Inst_12_15), .b(4'b0111), .eq(comparator_12_eq));  // open: gt, lt
  Comparator #(.width(4), .mode("unsigned")) comparator_13 (
    .a(Inst_12_15), .b(4'b1000), .eq(comparator_13_eq));  // open: gt, lt
  Comparator #(.width(4), .mode("unsigned")) comparator_14 (
    .a(Inst_12_15), .b(4'b1001), .eq(comparator_14_eq));  // open: gt, lt
  Comparator #(.width(4), .mode("unsigned")) comparator_15 (
    .a(Inst_12_15), .b(4'b1010), .eq(comparator_15_eq));  // open: gt, lt
  Comparator #(.width(4), .mode("unsigned")) comparator_16 (
    .a(Inst_12_15), .b(4'b0100), .eq(comparator_16_eq));  // open: gt, lt
  Comparator #(.width(4), .mode("unsigned")) comparator_17 (
    .a(Inst_12_15), .b(4'b0101), .eq(comparator_17_eq));  // open: gt, lt
  Comparator #(.width(4), .mode("unsigned")) comparator_18 (
    .a(Inst_12_15), .b(4'b1100), .eq(comparator_18_eq));  // open: gt, lt
  Comparator #(.width(4), .mode("unsigned")) comparator_19 (
    .a(Inst_12_15), .b(4'b0100), .eq(comparator_19_eq));  // open: gt, lt
  Comparator #(.width(4), .mode("unsigned")) comparator_20 (
    .a(Inst_12_15), .b(4'b0101), .eq(comparator_20_eq));  // open: gt, lt
  or or_1 (Jump, comparator_2_eq, comparator_3_eq);
  or or_2 (RegDst, comparator_4_eq, comparator_5_eq);
  or or_3 (ExtOpt, comparator_6_eq, comparator_7_eq);
  not not_5 (ALUSrc, comparator_8_eq);
  or or_4 (or_4_out, comparator_16_eq, comparator_17_eq, comparator_18_eq);
  or or_5 (Branch, comparator_19_eq, comparator_20_eq);
  and and_1 (and_1_out, not_2_out, Inst_12_15[2], Inst_12_15[1], Inst_12_15[0]);
  and and_2 (and_2_out, Inst_12_15[3], not_1_out, not_4_out);
  or or_6 (or_6_out, Inst_12_15[3], not_1_out, not_3_out, not_4_out);
  or or_7 (or_7_out, not_2_out, Inst_12_15[2], not_3_out, Inst_12_15[0]);
  and and_3 (and_3_out, not_2_out, Inst_12_15[2], Inst_12_15[1], Inst_12_15[0]);
  and and_4 (and_4_out, Inst_12_15[3], not_1_out, not_3_out, Inst_12_15[0]);
  not not_6 (RegWr, or_4_out);
  or or_8 (or_9_out[2], and_1_out, and_2_out);
  and and_5 (or_9_out[1], or_6_out, or_7_out);
  or or_9 (or_9_out[0], and_3_out, and_4_out);
  or or_10 (or_10_out, comparator_10_eq, comparator_11_eq, comparator_12_eq, comparator_13_eq, comparator_14_eq, comparator_15_eq);
  assign SrctoReg = or_10_out ? 2'b00 : 2'bz;  // Controlled_Buffer controlled_buffer_1
  Comparator #(.width(4), .mode("unsigned")) comparator_21 (
    .a(Inst_12_15), .b(4'b1011), .eq(comparator_21_eq));  // open: gt, lt
  assign SrctoReg = comparator_21_eq ? 2'b01 : 2'bz;  // Controlled_Buffer controlled_buffer_2
  Comparator #(.width(4), .mode("unsigned")) comparator_22 (
    .a(Inst_12_15), .b(4'b1011), .eq(comparator_22_eq));  // open: gt, lt
  assign SrctoReg = comparator_22_eq ? 2'b10 : 2'bz;  // Controlled_Buffer controlled_buffer_3
  Comparator #(.width(4), .mode("unsigned")) comparator_23 (
    .a(Inst_12_15), .b(4'b1011), .eq(comparator_23_eq));  // open: gt, lt
  assign SrctoReg = comparator_23_eq ? 2'b11 : 2'bz;  // Controlled_Buffer controlled_buffer_4
  Comparator #(.width(4), .mode("unsigned")) comparator_24 (
    .a(Inst_12_15), .b(4'b0000), .eq(comparator_24_eq));  // open: gt, lt
  Multiplexer #(.width(3), .enable("false")) multiplexer_1 (
    .in0(or_9_out), .in1(Inst__0_2), .out(ALUCtr), .sel(comparator_24_eq));

  // Other names for the same wires on the sheet: Inst_0_2[2:0] = Inst__0_2; D = Inst_12_15[0]; C = Inst_12_15[1];
  //   B = Inst_12_15[2]; A = Inst_12_15[3]
endmodule

module ExtendImm (
  input  [5:0] EIm,
  input  ExtOp,
  output [15:0] Immo
);

  wire [15:0] bit_extender_1_out, bit_extender_2_out;

  assign bit_extender_1_out = {{10{EIm[5]}}, EIm};  // Bit_Extender bit_extender_1
  assign bit_extender_2_out = {{10{1'b0}}, EIm};  // Bit_Extender bit_extender_2
  Multiplexer #(.width(16)) multiplexer_1 (
    .in0(bit_extender_1_out), .in1(bit_extender_2_out), .out(Immo), .sel(ExtOp));  // open: en
endmodule

module Hazard_Manage (
  input  [15:0] Instruction,
  input  Jump,
  input  Zero,
  input  Branch,
  output [15:0] Result
);

  wire and_1_out, or_1_out;
  wire [15:0] multiplexer_1_out;

  Multiplexer #(.width(16)) multiplexer_1 (
    .in0({16{1'b1}}), .in1({16{1'b0}}), .out(multiplexer_1_out), .sel(or_1_out));  // open: en
  or or_1 (or_1_out, Jump, and_1_out);
  and and_1 (and_1_out, Zero, Branch);
  assign Result = Instruction & multiplexer_1_out;  // AND_Gate and_2, 16 bits wide
endmodule

module LO_Input (
  input  [15:0] Result1,
  input  [9:0] Immediate,
  input  [2:0] funct,
  input  [3:0] Opt,
  output [15:0] To_LO
);

  wire comparator_1_eq, comparator_2_eq, f_0p, fb, not_1_out, not_2_out, not_3_out, op1, sb;
  wire [15:0] bit_extender_1_out, shifter_1_out;

  assign bit_extender_1_out = {{6{1'b0}}, Immediate};  // Bit_Extender bit_extender_1
  Shifter #(.width(16)) shifter_1 (.in(bit_extender_1_out), .\dist (4'b0110), .out(shifter_1_out));
  Comparator #(.width(3), .mode("unsigned")) comparator_1 (
    .a(funct), .b(3'b111), .eq(comparator_1_eq));  // open: gt, lt
  Comparator #(.width(4), .mode("unsigned")) comparator_2 (.a(4'b0000), .b(Opt), .eq(comparator_2_eq));  // open: gt, lt
  Comparator #(.width(4), .mode("unsigned")) comparator_3 (.a(Opt), .b(4'b0001), .eq(op1));  // open: gt, lt
  and and_1 (f_0p, comparator_1_eq, comparator_2_eq);
  and and_2 (fb, not_1_out, not_2_out);
  or or_1 (sb, not_3_out, op1);
  Multiplexer #(.select(2), .width(16)) multiplexer_1 (
    .in0(Result1), .in1(shifter_1_out), .in3({16{1'b0}}), .out(To_LO), .sel({fb, sb}));  // open: in2, en
  not not_1 (not_1_out, f_0p);
  not not_2 (not_2_out, op1);
  not not_3 (not_3_out, f_0p);

  // Other names for the same wires on the sheet: sel[1:0] = {fb, sb}
endmodule
