// Logisim project regfile.circ as structural Verilog: 1 circuit, main circuit main
module main (
  input  [2:0] Read_Register_1,
  input  [2:0] Read_Register_2,
  input  [2:0] Write_Register,
  input  [15:0] Write_Data,
  input  Write_Enable,
  input  Clock,
  output [15:0] s0_Value,
  output [15:0] s1_Value,
  output [15:0] s2_Value,
  output [15:0] ra_Value,
  output [15:0] sp_Value,
  output [15:0] Read_Data_1,
  output [15:0] Read_Data_2
);

  wire and_1_out, and_2_out, and_3_out, and_4_out, and_5_out, and_6_out, and_7_out, comparator_1_eq,
       comparator_2_eq, comparator_3_eq, comparator_4_eq, comparator_5_eq, comparator_6_eq, comparator_7_eq;
  wire [15:0] multiplexer_1_out, multiplexer_3_out, multiplexer_4_out, multiplexer_5_out, multiplexer_7_out,
       multiplexer_8_out, multiplexer_9_out, Read0, Read5, Read6;

  Register #(.width(16)) _0 (.Q(Read0), .clk(Clock));  // open: D, en, clr
  Multiplexer #(.width(16)) multiplexer_1 (
    .in0(ra_Value), .in1(Write_Data), .out(multiplexer_1_out), .sel(and_1_out));  // open: en
  and and_1 (and_1_out, comparator_1_eq, Write_Enable);
  Comparator #(.width(3)) comparator_1 (.a(3'b001), .b(Write_Register), .eq(comparator_1_eq));  // open: gt, lt
  Register #(.width(16)) _1 (.D(multiplexer_1_out), .Q(ra_Value), .clk(Clock));  // open: en, clr
  Multiplexer #(.select(3), .width(16)) multiplexer_2 (
    .in0(Read0), .in1(ra_Value), .in2(s0_Value), .in3(s1_Value), .in4(s2_Value), .in5(Read5), .in6(Read6),
    .in7(sp_Value), .out(Read_Data_1), .sel(Read_Register_1));  // open: en
  Multiplexer #(.width(16)) multiplexer_3 (
    .in0(sp_Value), .in1(Write_Data), .out(multiplexer_3_out), .sel(and_2_out));  // open: en
  and and_2 (and_2_out, comparator_2_eq, Write_Enable);
  Comparator #(.width(3)) comparator_2 (.a(3'b111), .b(Write_Register), .eq(comparator_2_eq));  // open: gt, lt
  Multiplexer #(.width(16)) multiplexer_4 (
    .in0(s0_Value), .in1(Write_Data), .out(multiplexer_4_out), .sel(and_3_out));  // open: en
  and and_3 (and_3_out, comparator_3_eq, Write_Enable);
  Comparator #(.width(3)) comparator_3 (.a(3'b010), .b(Write_Register), .eq(comparator_3_eq));  // open: gt, lt
  Register #(.width(16)) _7 (.D(multiplexer_3_out), .Q(sp_Value), .clk(Clock));  // open: en, clr
  Register #(.width(16)) _2 (.D(multiplexer_4_out), .Q(s0_Value), .clk(Clock));  // open: en, clr
  Multiplexer #(.width(16)) multiplexer_5 (
    .in0(s1_Value), .in1(Write_Data), .out(multiplexer_5_out), .sel(and_4_out));  // open: en
  Register #(.width(16)) _3 (.D(multiplexer_5_out), .Q(s1_Value), .clk(Clock));  // open: en, clr
  and and_4 (and_4_out, comparator_4_eq, Write_Enable);
  Comparator #(.width(3)) comparator_4 (.a(3'b011), .b(Write_Register), .eq(comparator_4_eq));  // open: gt, lt
  Multiplexer #(.select(3), .width(16)) multiplexer_6 (
    .in0(Read0), .in1(ra_Value), .in2(s0_Value), .in3(s1_Value), .in4(s2_Value), .in5(Read5), .in6(Read6),
    .in7(sp_Value), .out(Read_Data_2), .sel(Read_Register_2));  // open: en
  Multiplexer #(.width(16)) multiplexer_7 (
    .in0(s2_Value), .in1(Write_Data), .out(multiplexer_7_out), .sel(and_5_out));  // open: en
  Comparator #(.width(3)) comparator_5 (.a(3'b100), .b(Write_Register), .eq(comparator_5_eq));  // open: gt, lt
  Multiplexer #(.width(16)) multiplexer_8 (
    .in0(Read6), .in1(Write_Data), .out(multiplexer_8_out), .sel(and_6_out));  // open: en
  Comparator #(.width(3)) comparator_6 (.a(3'b110), .b(Write_Register), .eq(comparator_6_eq));  // open: gt, lt
  Register #(.width(16)) _4 (.D(multiplexer_7_out), .Q(s2_Value), .clk(Clock));  // open: en, clr
  and and_5 (and_5_out, comparator_5_eq, Write_Enable);
  Register #(.width(16)) _6 (.D(multiplexer_8_out), .Q(Read6), .clk(Clock));  // open: en, clr
  and and_6 (and_6_out, comparator_6_eq, Write_Enable);
  Register #(.width(16)) _5 (.D(multiplexer_9_out), .Q(Read5), .clk(Clock));  // open: en, clr
  Multiplexer #(.width(16)) multiplexer_9 (
    .in0(Read5), .in1(Write_Data), .out(multiplexer_9_out), .sel(and_7_out));  // open: en
  and and_7 (and_7_out, comparator_7_eq, Write_Enable);
  Comparator #(.width(3)) comparator_7 (.a(3'b101), .b(Write_Register), .eq(comparator_7_eq));  // open: gt, lt

  // Other names for the same wires on the sheet: clk = Clock; Read1[15:0] = ra_Value; Read2[15:0] = s0_Value;
  //   Read3[15:0] = s1_Value; Read4[15:0] = s2_Value; Read7[15:0] = sp_Value; read_data1[15:0] = Read_Data_1;
  //   read_data2[15:0] = Read_Data_2; read_reg1[2:0] = Read_Register_1; read_reg2[2:0] = Read_Register_2;
  //   write_en = Write_Enable; write_reg[2:0] = Write_Register

  // Notes on the sheet:
  //   INPUTS to your circuit
  //   DON'T CHANGE THE LOCATIONS OF THE INPUTS AND OUTPUTS!
  //   These are DEBUG/TEST outputs from your circuit.
  //   OUTPUTS from your circuit
endmodule
